# Fritzing sketch PIA (saved by Fritzing 0.9.3b)
circuit board: 3.86232cm x 3.89925cm
breadboards: 1

parts:
  Part1 = Arduino Mega ADK (Rev3)
  Rojo1 = LED - 5mm [color="Red (633nm)" package="5 mm [THT]"]
  Amar1 = LED - 5mm [color="Yellow (595nm)" package="5 mm [THT]"]
  Verde1 = LED - 5mm [color="Green (570nm)" package="5 mm [THT]"]
  Rojo2 = LED - 5mm [color="Red (633nm)" package="5 mm [THT]"]
  Amar2 = LED - 5mm [color="Yellow (595nm)" package="5 mm [THT]"]
  Verde2 = LED - 5mm [color="Green (570nm)" package="5 mm [THT]"]
  R2 = Resistor [tolerance=±5% resistance=220 package="2010 [SMD]"]
  R3 = Resistor [tolerance=±5% resistance=220 package="2010 [SMD]"]
  R4 = Resistor [tolerance=±5% resistance=220 package="2010 [SMD]"]
  R5 = Resistor [tolerance=±5% resistance=220 package="2010 [SMD]"]
  R6 = Resistor [tolerance=±5% resistance=220 package="2010 [SMD]"]
  R7 = Resistor [tolerance=±5% resistance=220 package="2010 [SMD]"]

nets:
  N1: Part1.D10_PWM, Rojo2.anode
  N2: Part1.D9_PWM, Amar2.anode
  N3: Part1.D8_PWM, Verde2.anode
  N4: Part1.GND, R2.Pin_1, R3.Pin_1, R4.Pin_1, R5.Pin_1, R6.Pin_1, R7.Pin_1
  N5: Part1.D5_PWM, Verde1.anode
  N6: Part1.D6_PWM, Amar1.anode
  N7: Part1.D7_PWM, Rojo1.anode
  N8: Rojo1.cathode, R6.Pin_0
  N9: Amar1.cathode, R5.Pin_0
  N10: Verde1.cathode, R4.Pin_0
  N11: Rojo2.cathode, R3.Pin_0
  N12: Amar2.cathode, R2.Pin_0
  N13: Verde2.cathode, R7.Pin_0

// code stored in the sketch: semaforo.ino
// Pines de arduino
int green1 = 5
int yellow1 = 6
int red1 = 7
int green2 = 8
int yellow2 = 9
int red2 = 10

void turnoff(led){
  // Apaga LED
  digitalWrite(led, LOW);
}
void turnon(led){
  // Prende LED
  digitalWrite(led, HIGH);
}
void switchled(ledoff,ledon,wait){
  // Apaga un led, prende otro y espera <wait> milisegundos
  turnoff(ledoff);
  turnon(ledon);
  sleep(wait);
}
void green2red(green,yellow,red){
  // Secuencia de verde a amarillo a rojo
  switchled(red,green,5000);
  switchled(green,yellow,1500);
  switchled(yellow,red,500);
}
void main(){
  // Define estado inicial e inicia secuencia de transformación de LEDs
  turnon(green1);
  turnon(red2);
  green2red(green1,yellow1,red1);
  green2red(green2,yellow2,red2);
}
void loop(){
  // Inicia programa en loop indefinidamente
  main();
}
